// Logisim project A2_grp1.circ as structural Verilog: 12 circuits, main circuit main
module main (
  input  [15:0] InputA,
  input  [15:0] InputB,
  output out_3,
  output out_4,
  output [15:0] out_5
);

  floatingPointAdder floatingpointadder_1 (
    .InputA(InputA), .InputB(InputB), .Overflow(out_3), .Underflow(out_4), .FinalAnswer(out_5));
endmodule

module rightShifter (
  input  [4:0] ExponentA,
  input  [4:0] ExponentB,
  input  [14:0] MantissaA,
  input  [14:0] MantissaB,
  output [4:0] ExpDiff,
  output [4:0] ExpLarger,
  output BisLarger
);

  wire or_1_out, subtractor_1_bout, subtractor_2_bout;
  wire [4:0] negator_1_out, subtractor_1_out;

  Subtractor #(.width(5)) subtractor_1 (
    .a(ExponentA), .b(ExponentB), .out(subtractor_1_out), .bout(subtractor_1_bout));  // open: bin
  Multiplexer #(.enable("true"), .width(5)) multiplexer_1 (
    .in0(ExponentA), .in1(ExponentB), .out(ExpLarger), .sel(subtractor_1_bout));  // open: en
  Subtractor #(.width(15)) subtractor_2 (.a(MantissaA), .b(MantissaB), .bout(subtractor_2_bout));  // open: out, bin
  Negator #(.width(5)) negator_1 (.in(subtractor_1_out), .out(negator_1_out));
  Multiplexer #(.enable("true"), .width(5)) multiplexer_2 (
    .in0(subtractor_1_out), .in1(negator_1_out), .out(ExpDiff), .sel(subtractor_1_bout));  // open: en
  Multiplexer multiplexer_3 (.in0(subtractor_2_bout), .in1(subtractor_1_bout), .out(BisLarger), .sel(or_1_out));
  or or_1 (or_1_out, ExpDiff[0], ExpDiff[1], ExpDiff[2], ExpDiff[3], ExpDiff[4]);
endmodule

module aligner (
  input  [4:0] ShiftAmount,
  input  [14:0] MantissaA,
  input  [14:0] MantissaB,
  input  BisLarger,
  input  SignA,
  input  SignB,
  output [14:0] MSmallerShifted,
  output [14:0] MLarger,
  output SLarger
);

  wire [3:0] multiplexer_1_out;
  wire [14:0] multiplexer_3_out;

  Multiplexer #(.width(4)) multiplexer_1 (
    .in0(ShiftAmount[3:0]), .in1(4'b1111), .out(multiplexer_1_out), .sel(ShiftAmount[4]));
  Multiplexer #(.enable("true"), .width(15)) multiplexer_2 (
    .in0(MantissaA), .in1(MantissaB), .out(MLarger), .sel(BisLarger));  // open: en
  Multiplexer #(.enable("true"), .width(15)) multiplexer_3 (
    .in0(MantissaB), .in1(MantissaA), .out(multiplexer_3_out), .sel(BisLarger));  // open: en
  Multiplexer #(.enable("true")) multiplexer_4 (.in0(SignA), .in1(SignB), .out(SLarger), .sel(BisLarger));  // open: en
  StickyBitRightShifter stickybitrightshifter_1 (
    .Shift_Amount_3d08ef0f(multiplexer_1_out), .Input(multiplexer_3_out), .Output(MSmallerShifted));
endmodule

module floatingPointAdder (
  input  [15:0] InputA,
  input  [15:0] InputB,
  output Overflow,
  output Underflow,
  output [15:0] FinalAnswer
);

  wire aligner_1_slarger, arithmetic_1_signresult, rightshifter_1_bislarger, unpacker2_1_signbit,
       unpacker2_2_signbit;
  wire [4:0] arithmetic_1_expresult, rightshifter_1_expdiff, rightshifter_1_explarger, unpacker2_1_exponent,
       unpacker2_2_exponent;
  wire [5:0] leftnormalizer_1_enormalized, rightnormalizer_1_erightnormalized, rounder_1_erounded;
  wire [9:0] rounder_1_mrounded;
  wire [14:0] aligner_1_mlarger, aligner_1_msmallershifted, leftnormalizer_1_mnormalized,
       rightnormalizer_1_mrightnormalized, unpacker2_1_mantissa, unpacker2_2_mantissa;
  wire [15:0] arithmetic_1_mresult;

  unpacker2 unpacker2_1 (
    .InputA(InputA), .Mantissa(unpacker2_1_mantissa), .Exponent(unpacker2_1_exponent),
    .SignBit(unpacker2_1_signbit));
  unpacker2 unpacker2_2 (
    .InputA(InputB), .Mantissa(unpacker2_2_mantissa), .Exponent(unpacker2_2_exponent),
    .SignBit(unpacker2_2_signbit));
  rightShifter rightshifter_1 (
    .ExponentA(unpacker2_1_exponent), .ExponentB(unpacker2_2_exponent), .MantissaA(unpacker2_1_mantissa),
    .MantissaB(unpacker2_2_mantissa), .ExpDiff(rightshifter_1_expdiff), .ExpLarger(rightshifter_1_explarger),
    .BisLarger(rightshifter_1_bislarger));
  aligner aligner_1 (
    .ShiftAmount(rightshifter_1_expdiff), .MantissaA(unpacker2_1_mantissa), .MantissaB(unpacker2_2_mantissa),
    .BisLarger(rightshifter_1_bislarger), .SignA(unpacker2_1_signbit), .SignB(unpacker2_2_signbit),
    .MSmallerShifted(aligner_1_msmallershifted), .MLarger(aligner_1_mlarger), .SLarger(aligner_1_slarger));
  arithmetic arithmetic_1 (
    .MLarger(aligner_1_mlarger), .Mshifted(aligner_1_msmallershifted), .SignLarger(aligner_1_slarger),
    .SignA(unpacker2_1_signbit), .ExpLarger(rightshifter_1_explarger), .SignB(unpacker2_2_signbit),
    .Mresult(arithmetic_1_mresult), .SignResult(arithmetic_1_signresult), .ExpResult(arithmetic_1_expresult));
  RightNormalizer rightnormalizer_1 (
    .MResult(arithmetic_1_mresult), .ExpResult(arithmetic_1_expresult),
    .MRightNormalized(rightnormalizer_1_mrightnormalized),
    .ERightNormalized(rightnormalizer_1_erightnormalized));
  LeftNormalizer leftnormalizer_1 (
    .MRightNormalized(rightnormalizer_1_mrightnormalized),
    .ERightNormalized(rightnormalizer_1_erightnormalized), .MNormalized(leftnormalizer_1_mnormalized),
    .ENormalized(leftnormalizer_1_enormalized));
  Rounder rounder_1 (
    .MNormalized(leftnormalizer_1_mnormalized), .ENormalized(leftnormalizer_1_enormalized),
    .MRounded(rounder_1_mrounded), .ERounded(rounder_1_erounded));
  Repacker repacker_1 (
    .Underflow(Underflow), .Overflow(Overflow), .MRounded(rounder_1_mrounded), .ERounded(rounder_1_erounded),
    .Sign(arithmetic_1_signresult), .Answer(FinalAnswer));
  Exception exception_1 (.Exponent(rounder_1_erounded), .Overflow(Overflow), .Underflow(Underflow));
endmodule

module unpacker2 (
  input  [15:0] InputA,
  output [14:0] Mantissa,
  output [4:0] Exponent,
  output SignBit
);


  assign Exponent = InputA[14:10];
  assign Mantissa = {1'b1, InputA[9:0], 4'b0000};
  assign SignBit = InputA[15];
endmodule

module StickyBitRightShifter (
  input  [3:0] Shift_Amount_3d08ef0f,
  input  [14:0] Input,
  output [14:0] Output
);

  wire or_1_out, or_2_out, or_3_out, or_4_out, or_5_out, or_6_out, or_7_out, or_8_out, or_9_out, or_10_out,
       or_11_out, or_12_out, or_13_out, or_14_out;

  Multiplexer #(.select(4)) multiplexer_1 (
    .in0(Input[14]), .in1(1'b0), .in2(1'b0), .in3(1'b0), .in4(1'b0), .in5(1'b0), .in6(1'b0), .in7(1'b0),
    .in8(1'b0), .in9(1'b0), .in10(1'b0), .in11(1'b0), .in12(1'b0), .in13(1'b0), .in14(1'b0), .in15(1'b0),
    .out(Output[14]), .sel(Shift_Amount_3d08ef0f));
  Multiplexer #(.select(4)) multiplexer_2 (
    .in0(Input[13]), .in1(Input[14]), .in2(1'b0), .in3(1'b0), .in4(1'b0), .in5(1'b0), .in6(1'b0), .in7(1'b0),
    .in8(1'b0), .in9(1'b0), .in10(1'b0), .in11(1'b0), .in12(1'b0), .in13(1'b0), .in14(1'b0), .in15(1'b0),
    .out(Output[13]), .sel(Shift_Amount_3d08ef0f));
  Multiplexer #(.select(4)) multiplexer_3 (
    .in0(Input[12]), .in1(Input[13]), .in2(Input[14]), .in3(1'b0), .in4(1'b0), .in5(1'b0), .in6(1'b0),
    .in7(1'b0), .in8(1'b0), .in9(1'b0), .in10(1'b0), .in11(1'b0), .in12(1'b0), .in13(1'b0), .in14(1'b0),
    .in15(1'b0), .out(Output[12]), .sel(Shift_Amount_3d08ef0f));
  Multiplexer #(.select(4)) multiplexer_4 (
    .in0(Input[11]), .in1(Input[12]), .in2(Input[13]), .in3(Input[14]), .in4(1'b0), .in5(1'b0), .in6(1'b0),
    .in7(1'b0), .in8(1'b0), .in9(1'b0), .in10(1'b0), .in11(1'b0), .in12(1'b0), .in13(1'b0), .in14(1'b0),
    .in15(1'b0), .out(Output[11]), .sel(Shift_Amount_3d08ef0f));
  Multiplexer #(.select(4)) multiplexer_5 (
    .in0(Input[10]), .in1(Input[11]), .in2(Input[12]), .in3(Input[13]), .in4(Input[14]), .in5(1'b0),
    .in6(1'b0), .in7(1'b0), .in8(1'b0), .in9(1'b0), .in10(1'b0), .in11(1'b0), .in12(1'b0), .in13(1'b0),
    .in14(1'b0), .in15(1'b0), .out(Output[10]), .sel(Shift_Amount_3d08ef0f));
  Multiplexer #(.select(4)) multiplexer_6 (
    .in0(Input[9]), .in1(Input[10]), .in2(Input[11]), .in3(Input[12]), .in4(Input[13]), .in5(Input[14]),
    .in6(1'b0), .in7(1'b0), .in8(1'b0), .in9(1'b0), .in10(1'b0), .in11(1'b0), .in12(1'b0), .in13(1'b0),
    .in14(1'b0), .in15(1'b0), .out(Output[9]), .sel(Shift_Amount_3d08ef0f));
  Multiplexer #(.select(4)) multiplexer_7 (
    .in0(Input[8]), .in1(Input[9]), .in2(Input[10]), .in3(Input[11]), .in4(Input[12]), .in5(Input[13]),
    .in6(Input[14]), .in7(1'b0), .in8(1'b0), .in9(1'b0), .in10(1'b0), .in11(1'b0), .in12(1'b0), .in13(1'b0),
    .in14(1'b0), .in15(1'b0), .out(Output[8]), .sel(Shift_Amount_3d08ef0f));
  Multiplexer #(.select(4)) multiplexer_8 (
    .in0(Input[7]), .in1(Input[8]), .in2(Input[9]), .in3(Input[10]), .in4(Input[11]), .in5(Input[12]),
    .in6(Input[13]), .in7(Input[14]), .in8(1'b0), .in9(1'b0), .in10(1'b0), .in11(1'b0), .in12(1'b0),
    .in13(1'b0), .in14(1'b0), .in15(1'b0), .out(Output[7]), .sel(Shift_Amount_3d08ef0f));
  Multiplexer #(.select(4)) multiplexer_9 (
    .in0(Input[6]), .in1(Input[7]), .in2(Input[8]), .in3(Input[9]), .in4(Input[10]), .in5(Input[11]),
    .in6(Input[12]), .in7(Input[13]), .in8(Input[14]), .in9(1'b0), .in10(1'b0), .in11(1'b0), .in12(1'b0),
    .in13(1'b0), .in14(1'b0), .in15(1'b0), .out(Output[6]), .sel(Shift_Amount_3d08ef0f));
  Multiplexer #(.select(4)) multiplexer_10 (
    .in0(Input[5]), .in1(Input[6]), .in2(Input[7]), .in3(Input[8]), .in4(Input[9]), .in5(Input[10]),
    .in6(Input[11]), .in7(Input[12]), .in8(Input[13]), .in9(Input[14]), .in10(1'b0), .in11(1'b0),
    .in12(1'b0), .in13(1'b0), .in14(1'b0), .in15(1'b0), .out(Output[5]), .sel(Shift_Amount_3d08ef0f));
  Multiplexer #(.select(4)) multiplexer_11 (
    .in0(Input[4]), .in1(Input[5]), .in2(Input[6]), .in3(Input[7]), .in4(Input[8]), .in5(Input[9]),
    .in6(Input[10]), .in7(Input[11]), .in8(Input[12]), .in9(Input[13]), .in10(Input[14]), .in11(1'b0),
    .in12(1'b0), .in13(1'b0), .in14(1'b0), .in15(1'b0), .out(Output[4]), .sel(Shift_Amount_3d08ef0f));
  Multiplexer #(.select(4)) multiplexer_12 (
    .in0(Input[3]), .in1(Input[4]), .in2(Input[5]), .in3(Input[6]), .in4(Input[7]), .in5(Input[8]),
    .in6(Input[9]), .in7(Input[10]), .in8(Input[11]), .in9(Input[12]), .in10(Input[13]), .in11(Input[14]),
    .in12(1'b0), .in13(1'b0), .in14(1'b0), .in15(1'b0), .out(Output[3]), .sel(Shift_Amount_3d08ef0f));
  Multiplexer #(.select(4)) multiplexer_13 (
    .in0(Input[2]), .in1(Input[3]), .in2(Input[4]), .in3(Input[5]), .in4(Input[6]), .in5(Input[7]),
    .in6(Input[8]), .in7(Input[9]), .in8(Input[10]), .in9(Input[11]), .in10(Input[12]), .in11(Input[13]),
    .in12(Input[14]), .in13(1'b0), .in14(1'b0), .in15(1'b0), .out(Output[2]), .sel(Shift_Amount_3d08ef0f));
  Multiplexer #(.select(4)) multiplexer_14 (
    .in0(Input[1]), .in1(Input[2]), .in2(Input[3]), .in3(Input[4]), .in4(Input[5]), .in5(Input[6]),
    .in6(Input[7]), .in7(Input[8]), .in8(Input[9]), .in9(Input[10]), .in10(Input[11]), .in11(Input[12]),
    .in12(Input[13]), .in13(Input[14]), .in14(1'b0), .in15(1'b0), .out(Output[1]), .sel(Shift_Amount_3d08ef0f));
  or or_1 (or_1_out, Input[0], Input[1]);
  or or_2 (or_2_out, or_1_out, Input[2]);
  or or_3 (or_3_out, or_2_out, Input[3]);
  or or_4 (or_4_out, or_3_out, Input[4]);
  or or_5 (or_5_out, or_4_out, Input[5]);
  or or_6 (or_6_out, or_5_out, Input[6]);
  or or_7 (or_7_out, or_6_out, Input[7]);
  or or_8 (or_8_out, or_7_out, Input[8]);
  or or_9 (or_9_out, or_8_out, Input[9]);
  or or_10 (or_10_out, or_9_out, Input[10]);
  or or_11 (or_11_out, or_10_out, Input[11]);
  or or_12 (or_12_out, or_11_out, Input[12]);
  or or_13 (or_13_out, or_12_out, Input[13]);
  or or_14 (or_14_out, or_13_out, Input[14]);
  Multiplexer #(.select(4)) multiplexer_15 (
    .in0(1'b0), .in1(Input[0]), .in2(or_1_out), .in3(or_2_out), .in4(or_3_out), .in5(or_4_out),
    .in6(or_5_out), .in7(or_6_out), .in8(or_7_out), .in9(or_8_out), .in10(or_9_out), .in11(or_10_out),
    .in12(or_11_out), .in13(or_12_out), .in14(or_13_out), .in15(or_14_out), .out(Output[0]),
    .sel(Shift_Amount_3d08ef0f));
endmodule

module arithmetic (
  input  [14:0] MLarger,
  input  [14:0] Mshifted,
  input  SignLarger,
  input  SignA,
  input  [4:0] ExpLarger,
  input  SignB,
  output [15:0] Mresult,
  output SignResult,
  output [4:0] ExpResult
);

  wire or_1_out, xor_1_out;
  wire [15:0] adder_1_out, subtractor_1_out;

  Adder #(.width(16)) adder_1 (.a({1'b0, MLarger}), .b({1'b0, Mshifted}), .out(adder_1_out));  // open: cin, cout
  Subtractor #(.width(16)) subtractor_1 (
    .a({1'b0, MLarger}), .b({1'b0, Mshifted}), .out(subtractor_1_out));  // open: bin, bout
  xor xor_1 (xor_1_out, SignA, SignB);
  Multiplexer #(.width(16)) multiplexer_1 (.in0(adder_1_out), .in1(subtractor_1_out), .out(Mresult), .sel(xor_1_out));
  Multiplexer multiplexer_2 (.in0(1'b0), .in1(SignLarger), .out(SignResult), .sel(or_1_out));
  Multiplexer #(.width(5)) multiplexer_3 (.in0({5{1'b0}}), .in1(ExpLarger), .out(ExpResult), .sel(or_1_out));
  or or_1 (or_1_out, Mresult[0], Mresult[1], Mresult[2], Mresult[3], Mresult[4], Mresult[5], Mresult[6], Mresult[7], Mresult[8], Mresult[9], Mresult[10], Mresult[11], Mresult[12], Mresult[13], Mresult[14], Mresult[15]);
endmodule

module RightNormalizer (
  input  [15:0] MResult,
  input  [4:0] ExpResult,
  output [14:0] MRightNormalized,
  output [5:0] ERightNormalized
);

  wire [0:0] or_1_out;
  wire [5:0] adder_1_out;
  wire [15:0] shifter_1_out;
  wire [15:15] multiplexer_2_out;

  or or_1 (or_1_out[0], MResult[0], MResult[1]);
  Shifter #(.shift("lr"), .width(16)) shifter_1 (.in(MResult), .\dist (4'b0001), .out(shifter_1_out));
  Adder #(.width(6)) adder_1 (.a({1'b0, ExpResult}), .b(6'b000001), .out(adder_1_out));  // open: cin, cout
  Multiplexer #(.width(6)) multiplexer_1 (
    .in0({1'b0, ExpResult}), .in1(adder_1_out), .out(ERightNormalized), .sel(MResult[15]));
  Multiplexer #(.width(16)) multiplexer_2 (
    .in0(MResult), .in1({shifter_1_out[15:1], or_1_out[0]}), .out({multiplexer_2_out[15], MRightNormalized}),
    .sel(MResult[15]));
endmodule

module LeftNormalizer (
  input  [14:0] MRightNormalized,
  input  [5:0] ERightNormalized,
  output [14:0] MNormalized,
  output [5:0] ENormalized
);

  wire priority_encoder_1_gs;
  wire [3:0] priority_encoder_1_out, subtractor_2_out;
  wire [5:0] bit_extender_1_out, subtractor_1_out;
  wire [14:0] shifter_1_out;

  Subtractor #(.width(6)) subtractor_1 (
    .a(ERightNormalized), .b(bit_extender_1_out), .out(subtractor_1_out));  // open: bin, bout
  Priority_Encoder #(.select(4)) priority_encoder_1 (
    .in0(MRightNormalized[0]), .in1(MRightNormalized[1]), .in2(MRightNormalized[2]),
    .in3(MRightNormalized[3]), .in4(MRightNormalized[4]), .in5(MRightNormalized[5]),
    .in6(MRightNormalized[6]), .in7(MRightNormalized[7]), .in8(MRightNormalized[8]),
    .in9(MRightNormalized[9]), .in10(MRightNormalized[10]), .in11(MRightNormalized[11]),
    .in12(MRightNormalized[12]), .in13(MRightNormalized[13]), .in14(MRightNormalized[14]),
    .out(priority_encoder_1_out), .gs(priority_encoder_1_gs));  // open: in15, en_out, en_in
  Multiplexer #(.width(15)) multiplexer_1 (
    .in0(MRightNormalized), .in1(shifter_1_out), .out(MNormalized), .sel(priority_encoder_1_gs));
  assign bit_extender_1_out = {{2{1'b0}}, subtractor_2_out};  // Bit_Extender bit_extender_1
  Subtractor #(.width(4)) subtractor_2 (
    .a(4'b1110), .b(priority_encoder_1_out), .out(subtractor_2_out));  // open: bin, bout
  Shifter #(.width(15)) shifter_1 (.in(MRightNormalized), .\dist (subtractor_2_out), .out(shifter_1_out));
  Multiplexer #(.width(6)) multiplexer_2 (
    .in0(ERightNormalized), .in1(subtractor_1_out), .out(ENormalized), .sel(priority_encoder_1_gs));
endmodule

module Rounder (
  input  [14:0] MNormalized,
  input  [5:0] ENormalized,
  output [9:0] MRounded,
  output [5:0] ERounded
);

  wire adder_2_cout, and_1_out, or_1_out, or_2_out;
  wire [5:0] bit_extender_1_out;
  wire [9:0] bit_extender_2_out;

  Adder #(.width(6)) adder_1 (.a(bit_extender_1_out), .b(ENormalized), .out(ERounded));  // open: cin, cout
  or or_1 (or_1_out, MNormalized[0], MNormalized[1]);
  or or_2 (or_2_out, or_1_out, MNormalized[2]);
  and and_1 (and_1_out, or_2_out, MNormalized[3]);
  assign bit_extender_1_out = {{5{1'b0}}, adder_2_cout};  // Bit_Extender bit_extender_1
  assign bit_extender_2_out = {{9{1'b0}}, and_1_out};  // Bit_Extender bit_extender_2
  Adder #(.width(10)) adder_2 (
    .a(bit_extender_2_out), .b(MNormalized[13:4]), .out(MRounded), .cout(adder_2_cout));  // open: cin
endmodule

module Repacker (
  input  Underflow,
  input  Overflow,
  input  [9:0] MRounded,
  input  [5:0] ERounded,
  input  Sign,
  output [15:0] Answer
);

  wire or_1_out;
  wire [4:0] multiplexer_2_out;

  or or_1 (or_1_out, Underflow, Overflow);
  Multiplexer #(.width(10)) multiplexer_1 (.in0(MRounded), .in1({10{1'b0}}), .out(Answer[9:0]), .sel(or_1_out));
  Multiplexer #(.width(5)) multiplexer_2 (
    .in0(ERounded[4:0]), .in1({5{1'b0}}), .out(multiplexer_2_out), .sel(Underflow));
  Multiplexer #(.width(5)) multiplexer_3 (
    .in0(multiplexer_2_out), .in1({5{1'b1}}), .out(Answer[14:10]), .sel(Overflow));

  assign Answer[15] = Sign;
endmodule

module Exception (
  input  [5:0] Exponent,
  output Overflow,
  output Underflow
);

  wire comparator_2_eq, comparator_2_lt, not_1_out, or_1_out;

  Comparator #(.mode("unsigned"), .width(6)) comparator_1 (.a(Exponent), .b(6'b011110), .gt(Overflow));  // open: eq, lt
  Comparator #(.width(6)) comparator_2 (
    .a(Exponent), .b({6{1'b0}}), .eq(comparator_2_eq), .lt(comparator_2_lt));  // open: gt
  or or_1 (or_1_out, comparator_2_eq, comparator_2_lt);
  not not_1 (not_1_out, Overflow);
  and and_1 (Underflow, not_1_out, or_1_out);
endmodule
